# Fritzing sketch coopDoor (saved by Fritzing 0.9.4)
breadboards: 1

parts:
  Parça1 = Arduino Uno (Rev3)
  Parça2 = Bluetooth HC-05 Macho
  S2 = Pushbutton [package="[SMD]"]
  R1 = Resistor [tolerance=±5% resistance=10k package=THT]
  J1 = Basic Servo
  VCC1 = Battery
  VCC2 = Battery
  VCC3 = Battery

nets:
  N1: Parça1.A0, Parça2.RXD
  N2: Parça1.A1, Parça2.TXD
  N3: Parça1.D9_PWM, J1.pulse
  N4: Parça1.GND, R1.Pin_1
  N5: Parça1.D4, S2.Pin_1, S2.Pin_2, R1.Pin_0
  5V: Parça1.5V, Parça2.VCC
  N6: Parça1.VIN, S2.Pin_3, S2.Pin_4
  GND: Parça2.GND, J1.gnd, VCC3.-
  N7: J1.vcc, VCC1.+
  N8: VCC1.-, VCC2.+
  N9: VCC2.-, VCC3.+

// code stored in the sketch: CoopDoor.h
#include <Servo.h>
#include <SoftwareSerial.h>

using namespace std;

class PoultryDoor {

  private:
    Servo Engine;
    

  public:
    bool isOpened = false;
    int pin;
    PoultryDoor(int doorPin) {
      this->pin = doorPin;
    }

    void _setup(){
      this->_close();
      this->Engine.attach(this->pin);
    }

    void _open() {
      
      if (!this->isOpened) {
        this->Engine.write(180);
        this->isOpened = true;
      }
    }

    void _close() {
      if (this->isOpened) {
        this->Engine.write(90);
        this->isOpened = false;
      }
    }
};

// code stored in the sketch: coopDoor.ino
#include "CoopDoor.h"

int TX = A0;
int RX = A1;
SoftwareSerial BTSerial(RX, TX);

int buttonPin=4;


/**
  which recieved data
*/
String data;

CoopDoor theDoor(9);

void setup() {
  // put your setup code here, to run once:
  BTSerial.begin(38400);
  theDoor._setup();
  pinMode(buttonPin,INPUT);
	Serial.begin(9600);
}

void loop() {
  // put your main code here, to run repeatedly:
  if (BTSerial.available()) {
    data = BTSerial.readString();
    Serial.println(data);
    if (data == "Aç") {
			Serial.println("aç?l?yor");
      theDoor._open();
    } else if (data == "Kapat") {
      theDoor._close();
    }
  }else if(digitalRead(buttonPin) == 1){
    theDoor._open();
    delay(200);
  }
}
